# Fritzing sketch Esp8266 with EEPROM (saved by Fritzing 0.9.3b)
breadboards: 1

parts:
  U1 = NodeMCU V1.0
  OLED1 = SSD1306 0.96in 128x64 I2C Monochrome OLED Display

nets:
  N1: U1.D1, OLED1.SCL
  N2: U1.D2, OLED1.SDA
  GND: U1.GND, OLED1.GND
  VIN: U1.Vin, OLED1.VCC

custom parts:
  NodeMCU V1.0: ESP8266 based NodeMCU
