# Fritzing sketch esp-weatherstation&MQ7 (saved by Fritzing 0.9.3b)
breadboards: 1

parts:
  U1 = NodeMCU V1.0
  DHT1 = DHT22 Humidity and Temperature Sensor
  Part1 = MQ-7 breakout

nets:
  GND: U1.GND, DHT1.GND, Part1.GND
  N1: U1.D5, DHT1.DATA
  VIN: U1.Vin, DHT1.VDD, Part1.VCC
  N2: U1.A0, Part1.AO

custom parts:
  NodeMCU V1.0: ESP8266 based NodeMCU
  MQ-7 breakout: SKU: 101282
